// Logisim project 8bit_cpu.circ as structural Verilog: 7 circuits, main circuit main
module main (
  input  [15:0] in_1,
  input  in_2,
  output [15:0] PC,
  output [31:0] out_4,
  output ZERO,
  output ODD_PARITY,
  output EVEN_PARITY,
  output CARRY,
  output OVERFLOW
);

  wire and_1_out, Clock, not_1_out, or_1_out, PC_Shift_out, PC_Shift_q2, R_W_Shift_out, RESET,
       shift_register_1_out, shift_register_1_q0, sycronizer_out, Syncronize, xor_1_out;
  wire [3:0] IR_q_2;
  wire [11:0] IR_q;
  wire [15:0] MAR_q, MBR_q, RA_q, RB_q, register_bank_1_data_out__8_bits, register_bank_1_data_out__8_bits_2,
       rom_1_data;
  wire [31:0] RZ_q;

  pc pc_1 (.PC_In(in_1), .Clock(Clock), .PC_Enable(PC_Shift_out), .Reset(RESET), .out_5(PC));
  Register #(.width(16)) MAR (.D(PC), .en(PC_Shift_out), .Q(MAR_q), .clk(Clock), .clr(RESET));
  and and_1 (and_1_out, not_1_out, Syncronize);
  Shift_Register #(.length(3)) sycronizer (
    .shift(and_1_out), .in(sycronizer_out), .clk(Clock), .out(sycronizer_out));  // open: load, clr, d0, q0, d1, q1, d2, q2
  Register #(.width(16)) MBR (.D(rom_1_data), .Q(MBR_q), .clk(Clock), .clr(RESET));  // open: en
  ROM #(.addrWidth(16), .dataWidth(16)) rom_1 (.addr(MAR_q), .data(rom_1_data));  // open: sel
  Shift_Register #(.length(4)) R_W_Shift (
    .shift(shift_register_1_out), .in(R_W_Shift_out), .clk(Clock), .out(R_W_Shift_out));  // open: load, clr, d0, q0, d1, q1, d2, q2, d3, q3
  not not_1 (not_1_out, PC_Shift_q2);
  Register #(.width(16)) IR (.D(MBR_q), .Q({IR_q_2, IR_q}), .clk(Clock), .clr(RESET));  // open: en
  Shift_Register #(.length(2)) shift_register_1 (
    .in(or_1_out), .clk(Clock), .out(shift_register_1_out), .q0(shift_register_1_q0));  // open: shift, load, clr, d0, d1, q1
  Shift_Register #(.length(3)) PC_Shift (
    .shift(xor_1_out), .in(PC_Shift_out), .clk(Clock), .out(PC_Shift_out), .q2(PC_Shift_q2));  // open: load, clr, d0, q0, d1, q1, d2
  or or_1 (or_1_out, shift_register_1_out, shift_register_1_q0);
  register_bank register_bank_1 (
    .Data_in__16_bits(RZ_q[15:0]), .Rx__4_bits(IR_q[3:0]), .Rx__4_bits_2(IR_q[11:8]), .Clock(Clock),
    .R_W_prime(R_W_Shift_out), .Data_out__8_bits(register_bank_1_data_out__8_bits),
    .Data_out__8_bits_2(register_bank_1_data_out__8_bits_2));
  xor xor_1 (xor_1_out, sycronizer_out, in_2);
  Button button_1 (.out(RESET));
  Register #(.width(16)) RB (.D(register_bank_1_data_out__8_bits_2), .Q(RB_q), .clk(Clock), .clr(RESET));  // open: en
  Register #(.width(16)) RA (.D(register_bank_1_data_out__8_bits), .Q(RA_q), .clk(Clock), .clr(RESET));  // open: en
  Button button_2 (.out(Clock));
  Hex_Digit_Display hex_digit_display_1 (.value(out_4[27:24]));  // open: dp
  Hex_Digit_Display hex_digit_display_2 (.value(out_4[31:28]));  // open: dp
  Register #(.width(32)) RZ (.D(out_4), .Q(RZ_q), .clk(Clock), .clr(RESET));  // open: en
  _16_bit_alu u_16_bit_alu_1 (
    .A(RA_q), .B(RB_q), .SELECT(IR_q_2), .ALU_output(out_4), .ZERO_FO(ZERO), .out_6(ODD_PARITY),
    .out_7(EVEN_PARITY));
  Hex_Digit_Display hex_digit_display_3 (.value(out_4[19:16]));  // open: dp
  Hex_Digit_Display hex_digit_display_4 (.value(out_4[23:20]));  // open: dp
  Shift_Register #(.length(4)) shift_register_2 (
    .in(1'b1), .clk(Clock), .out(Syncronize), .clr(RESET));  // open: shift, load, d0, q0, d1, q1, d2, q2, d3, q3
  Hex_Digit_Display hex_digit_display_5 (.value(out_4[15:12]));  // open: dp
  Hex_Digit_Display hex_digit_display_6 (.value(out_4[7:4]));  // open: dp
  Hex_Digit_Display hex_digit_display_7 (.value(out_4[11:8]));  // open: dp
  PSW psw_1 (.in_1(RZ_q[31:16]), .in_2(IR_q_2), .CARRY(CARRY), .borrow(OVERFLOW));
  Hex_Digit_Display hex_digit_display_8 (.value(out_4[3:0]));  // open: dp

  // Notes on the sheet:
  //   Code Memory
  //   contents of rom_1 (hex, n*v repeats v):
  //   4102 3405 3607 2708
  //   16-BIT-REGISTER-BANK
  //   Result
  //   16-BIT-ALU
  //   PSW
endmodule

module register_bank (
  input  [15:0] Data_in__16_bits,
  input  [3:0] Rx__4_bits,
  input  [3:0] Rx__4_bits_2,
  input  Clock,
  input  R_W_prime,
  output [15:0] Data_out__8_bits,
  output [15:0] Data_out__8_bits_2
);

  wire decoder_1_out0, decoder_1_out1, decoder_1_out2, decoder_1_out3, decoder_1_out4, decoder_1_out5,
       decoder_1_out6, decoder_1_out7, decoder_1_out8, decoder_1_out9, decoder_1_out10, decoder_1_out11,
       decoder_1_out12, decoder_1_out13, decoder_1_out14, decoder_1_out15, not_1_out;
  wire [15:0] R0_q, R1_q, R2_q, R3_q, R4_q, R5_q, R6_q, R7_q, R8_q, R9_q, R10_q, R11_q, R12_q, R13_q, R14_q,
       R15_q;

  not not_1 (not_1_out, R_W_prime);
  Decoder #(.select(4), .disabled(0)) decoder_1 (
    .out0(decoder_1_out0), .out1(decoder_1_out1), .out2(decoder_1_out2), .out3(decoder_1_out3),
    .out4(decoder_1_out4), .out5(decoder_1_out5), .out6(decoder_1_out6), .out7(decoder_1_out7),
    .out8(decoder_1_out8), .out9(decoder_1_out9), .out10(decoder_1_out10), .out11(decoder_1_out11),
    .out12(decoder_1_out12), .out13(decoder_1_out13), .out14(decoder_1_out14), .out15(decoder_1_out15),
    .sel(Rx__4_bits_2), .en(not_1_out));
  Register #(.width(16)) R0 (.D(Data_in__16_bits), .en(decoder_1_out0), .Q(R0_q), .clk(Clock));  // open: clr
  Register #(.width(16)) R1 (.D(Data_in__16_bits), .en(decoder_1_out1), .Q(R1_q), .clk(Clock));  // open: clr
  Register #(.width(16)) R2 (.D(Data_in__16_bits), .en(decoder_1_out2), .Q(R2_q), .clk(Clock));  // open: clr
  Register #(.width(16)) R3 (.D(Data_in__16_bits), .en(decoder_1_out3), .Q(R3_q), .clk(Clock));  // open: clr
  Register #(.width(16)) R4 (.D(Data_in__16_bits), .en(decoder_1_out4), .Q(R4_q), .clk(Clock));  // open: clr
  Register #(.width(16)) R5 (.D(Data_in__16_bits), .en(decoder_1_out5), .Q(R5_q), .clk(Clock));  // open: clr
  Register #(.width(16)) R6 (.D(Data_in__16_bits), .en(decoder_1_out6), .Q(R6_q), .clk(Clock));  // open: clr
  Register #(.width(16)) R7 (.D(Data_in__16_bits), .en(decoder_1_out7), .Q(R7_q), .clk(Clock));  // open: clr
  Register #(.width(16)) R8 (.D(Data_in__16_bits), .en(decoder_1_out8), .Q(R8_q), .clk(Clock));  // open: clr
  Register #(.width(16)) R9 (.D(Data_in__16_bits), .en(decoder_1_out9), .Q(R9_q), .clk(Clock));  // open: clr
  Register #(.width(16)) R10 (.D(Data_in__16_bits), .en(decoder_1_out10), .Q(R10_q), .clk(Clock));  // open: clr
  Register #(.width(16)) R11 (.D(Data_in__16_bits), .en(decoder_1_out11), .Q(R11_q), .clk(Clock));  // open: clr
  Register #(.width(16)) R12 (.D(Data_in__16_bits), .en(decoder_1_out12), .Q(R12_q), .clk(Clock));  // open: clr
  Register #(.width(16)) R13 (.D(Data_in__16_bits), .en(decoder_1_out13), .Q(R13_q), .clk(Clock));  // open: clr
  Register #(.width(16)) R14 (.D(Data_in__16_bits), .en(decoder_1_out14), .Q(R14_q), .clk(Clock));  // open: clr
  Register #(.width(16)) R15 (.D(Data_in__16_bits), .en(decoder_1_out15), .Q(R15_q), .clk(Clock));  // open: clr
  Hex_Digit_Display hex_digit_display_1 (.value(Data_out__8_bits[15:12]));  // open: dp
  Multiplexer #(.select(4), .width(16)) multiplexer_1 (
    .in0(R0_q), .in1(R1_q), .in2(R2_q), .in3(R3_q), .in4(R4_q), .in5(R5_q), .in6(R6_q), .in7(R7_q),
    .in8(R8_q), .in9(R9_q), .in10(R10_q), .in11(R11_q), .in12(R12_q), .in13(R13_q), .in14(R14_q),
    .in15(R15_q), .out(Data_out__8_bits), .sel(Rx__4_bits_2), .en(R_W_prime));
  Multiplexer #(.select(4), .width(16)) multiplexer_2 (
    .in0(R0_q), .in1(R1_q), .in2(R2_q), .in3(R3_q), .in4(R4_q), .in5(R5_q), .in6(R6_q), .in7(R7_q),
    .in8(R8_q), .in9(R9_q), .in10(R10_q), .in11(R11_q), .in12(R12_q), .in13(R13_q), .in14(R14_q),
    .in15(R15_q), .out(Data_out__8_bits_2), .sel(Rx__4_bits), .en(R_W_prime));
  Hex_Digit_Display hex_digit_display_2 (.value(Data_out__8_bits[11:8]));  // open: dp
  Hex_Digit_Display hex_digit_display_3 (.value(Data_out__8_bits[7:4]));  // open: dp
  Hex_Digit_Display hex_digit_display_4 (.value(Data_out__8_bits[3:0]));  // open: dp

  // Notes on the sheet:
  //   16-bit Register File (R0-R7)
endmodule

module _16_bit_alu (
  input  [15:0] A,
  input  [15:0] B,
  input  [3:0] SELECT,
  output [31:0] ALU_output,
  output ZERO_FO,
  output out_6,
  output out_7
);

  wire adder_1_cout, or_2_out, subtractor_1_bout;
  wire [3:0] bit_extender_2_out;
  wire [15:0] adder_1_out, adder_2_out, and_1_out, bit_extender_1_out, bit_extender_5_out,
       bit_extender_6_out, divider_1_out, divider_1_rem, multiplier_1_cout, multiplier_1_out, not_1_out,
       or_1_out, shifter_1_out, shifter_2_out, shifter_3_out, shifter_4_out, subtractor_1_out,
       subtractor_2_out;
  wire [31:0] bit_extender_3_out, bit_extender_4_out, bit_extender_7_out, bit_extender_8_out,
       bit_extender_9_out, bit_extender_10_out, bit_extender_11_out, bit_extender_12_out,
       bit_extender_13_out, bit_extender_14_out, bit_extender_15_out;

  assign bit_extender_1_out = {{15{1'b0}}, 1'b1};  // Bit_Extender bit_extender_1
  Bit_Extender #(.in_width(16), .out_width(4)) bit_extender_2 (.in(B), .out(bit_extender_2_out));
  assign bit_extender_3_out = {{16{1'b0}}, B};  // Bit_Extender bit_extender_3
  assign bit_extender_4_out = {{16{1'b0}}, A};  // Bit_Extender bit_extender_4
  Adder #(.width(16)) adder_1 (.a(A), .b(B), .out(adder_1_out), .cout(adder_1_cout));  // open: cin
  Subtractor #(.width(16)) subtractor_1 (.a(A), .b(B), .out(subtractor_1_out), .bout(subtractor_1_bout));  // open: bin
  Multiplier #(.width(16)) multiplier_1 (.a(A), .b(B), .out(multiplier_1_out), .cout(multiplier_1_cout));  // open: cin
  Divider #(.width(16)) divider_1 (.a(A), .b(B), .out(divider_1_out), .rem(divider_1_rem));  // open: upper
  Adder #(.width(16)) adder_2 (.a(A), .b(bit_extender_1_out), .out(adder_2_out));  // open: cin, cout
  Subtractor #(.width(16)) subtractor_2 (.a(A), .b(bit_extender_1_out), .out(subtractor_2_out));  // open: bin, bout
  assign and_1_out = A & B;  // AND_Gate and_1, 16 bits wide
  assign or_1_out = A | B;  // OR_Gate or_1, 16 bits wide
  assign not_1_out = ~A;  // NOT_Gate not_1, 16 bits wide
  Shifter #(.width(16), .shift("lr")) shifter_1 (.in(A), .\dist (bit_extender_2_out), .out(shifter_1_out));
  Shifter #(.width(16)) shifter_2 (.in(A), .\dist (bit_extender_2_out), .out(shifter_2_out));
  Shifter #(.width(16), .shift("rr")) shifter_3 (.in(A), .\dist (bit_extender_2_out), .out(shifter_3_out));
  Shifter #(.width(16), .shift("rl")) shifter_4 (.in(A), .\dist (bit_extender_2_out), .out(shifter_4_out));
  assign bit_extender_5_out = {{15{1'b0}}, adder_1_cout};  // Bit_Extender bit_extender_5
  assign bit_extender_6_out = {{15{1'b0}}, subtractor_1_bout};  // Bit_Extender bit_extender_6
  assign bit_extender_7_out = {{16{1'b0}}, adder_2_out};  // Bit_Extender bit_extender_7
  assign bit_extender_8_out = {{16{1'b0}}, subtractor_2_out};  // Bit_Extender bit_extender_8
  assign bit_extender_9_out = {{16{1'b0}}, and_1_out};  // Bit_Extender bit_extender_9
  assign bit_extender_10_out = {{16{1'b0}}, or_1_out};  // Bit_Extender bit_extender_10
  assign bit_extender_11_out = {{16{1'b0}}, not_1_out};  // Bit_Extender bit_extender_11
  assign bit_extender_12_out = {{16{1'b0}}, shifter_1_out};  // Bit_Extender bit_extender_12
  assign bit_extender_13_out = {{16{1'b0}}, shifter_2_out};  // Bit_Extender bit_extender_13
  assign bit_extender_14_out = {{16{1'b0}}, shifter_3_out};  // Bit_Extender bit_extender_14
  assign bit_extender_15_out = {{16{1'b0}}, shifter_4_out};  // Bit_Extender bit_extender_15
  Multiplexer #(.select(4), .width(32), .disabled(0)) multiplexer_1 (
    .in0(bit_extender_3_out), .in1(bit_extender_4_out), .in2({bit_extender_5_out, adder_1_out}),
    .in3({bit_extender_6_out, subtractor_1_out}), .in4({multiplier_1_cout, multiplier_1_out}),
    .in5({divider_1_rem, divider_1_out}), .in6(bit_extender_7_out), .in7(bit_extender_8_out),
    .in8(bit_extender_9_out), .in9(bit_extender_10_out), .in10(bit_extender_11_out), .in11({A, B}),
    .in12(bit_extender_12_out), .in13(bit_extender_13_out), .in14(bit_extender_14_out),
    .in15(bit_extender_15_out), .out(ALU_output), .sel(SELECT));  // open: en
  not not_2 (ZERO_FO, or_2_out);
  or or_2 (or_2_out, ALU_output[0], ALU_output[1], ALU_output[2], ALU_output[3], ALU_output[4], ALU_output[5], ALU_output[6], ALU_output[7], ALU_output[8], ALU_output[9], ALU_output[10], ALU_output[11], ALU_output[12], ALU_output[13], ALU_output[14], ALU_output[15], ALU_output[16], ALU_output[17], ALU_output[18], ALU_output[19], ALU_output[20], ALU_output[21], ALU_output[22], ALU_output[23], ALU_output[24], ALU_output[25], ALU_output[26], ALU_output[27], ALU_output[28], ALU_output[29], ALU_output[30], ALU_output[31]);
  xor odd_parity_1 (out_6, ALU_output[0], ALU_output[1], ALU_output[2], ALU_output[3], ALU_output[4], ALU_output[5], ALU_output[6], ALU_output[7], ALU_output[8], ALU_output[9], ALU_output[10], ALU_output[11], ALU_output[12], ALU_output[13], ALU_output[14], ALU_output[15], ALU_output[16], ALU_output[17], ALU_output[18], ALU_output[19], ALU_output[20], ALU_output[21], ALU_output[22], ALU_output[23], ALU_output[24], ALU_output[25], ALU_output[26], ALU_output[27], ALU_output[28], ALU_output[29], ALU_output[30], ALU_output[31]);
  xnor even_parity_1 (out_7, ALU_output[0], ALU_output[1], ALU_output[2], ALU_output[3], ALU_output[4], ALU_output[5], ALU_output[6], ALU_output[7], ALU_output[8], ALU_output[9], ALU_output[10], ALU_output[11], ALU_output[12], ALU_output[13], ALU_output[14], ALU_output[15], ALU_output[16], ALU_output[17], ALU_output[18], ALU_output[19], ALU_output[20], ALU_output[21], ALU_output[22], ALU_output[23], ALU_output[24], ALU_output[25], ALU_output[26], ALU_output[27], ALU_output[28], ALU_output[29], ALU_output[30], ALU_output[31]);

  // Notes on the sheet:
  //   BitExtender
  //   Increment-----------------------------
  //   Decrement-----------------------
  //   Exchange
  //   Load
  //   Store
  //   Add
  //   Sub
  //   Mul
  //   Div
  //   And
  //   OR
  //   ShiftRight
  //   ShiftLeft
  //   Rotateright
  //   RotateLeft
  //   ALU-8bit 
  //   Not
endmodule

module pc (
  input  [15:0] PC_In,
  input  Clock,
  input  PC_Enable,
  input  Reset,
  output [15:0] out_5
);

  wire [15:0] adder_1_out;

  Adder #(.width(16)) adder_1 (.a(PC_In), .b(out_5), .out(adder_1_out), .cin(1'b1));  // open: cout
  Register #(.width(16)) register_1 (.D(adder_1_out), .en(PC_Enable), .Q(out_5), .clk(Clock), .clr(Reset));
endmodule

module test (
  input  in_1,
  input  in_2,
  input  in_3,
  input  in_4,
  input  in_5,
  output out_6
);

  wire button_1_out, clock_1_out, clock_2_out, not_1_out, or_1_out, PC_Shift_2_out, PC_Shift_2_q2,
       PC_Shift_out, shift_register_1_q1, shift_register_2_out, shift_register_2_q0, shift_register_3_out,
       shift_register_4_out, shift_register_5_q4, undriven, undriven_2, xor_1_out;

  // Probe on in_4
  Shifter shifter_1 ();  // open: in, dist, out
  Clock clock_1 (.out(clock_1_out));
  Clock clock_2 (.out(clock_2_out));
  not not_1 (not_1_out, PC_Shift_2_q2);
  Shift_Register #(.length(3)) PC_Shift (
    .shift(not_1_out), .in(PC_Shift_out), .clk(button_1_out), .out(PC_Shift_out));  // open: load, clr, d0, q0, d1, q1, d2, q2
  Shift_Register shift_register_1 (
    .in(out_6), .clk(clock_1_out), .out(out_6), .load(undriven_2), .q1(shift_register_1_q1));  // open: shift, clr, d0, q0, d1, d2, q2, d3, q3, d4, q4, d5, q5, d6, q6, d7, q7
  Register register_1 (.en(undriven));  // open: D, Q, clk, clr
  Shift_Register #(.length(2)) shift_register_2 (
    .in(or_1_out), .clk(clock_2_out), .out(shift_register_2_out), .d0(in_4), .q0(shift_register_2_q0),
    .d1(in_4));  // open: shift, load, clr, q1
  Button button_1 (.out(button_1_out));
  Shift_Register #(.length(3)) PC_Shift_2 (
    .shift(xor_1_out), .in(PC_Shift_2_out), .clk(button_1_out), .out(PC_Shift_2_out), .q2(PC_Shift_2_q2));  // open: load, clr, d0, q0, d1, q1, d2
  Shift_Register #(.length(6)) shift_register_3 (
    .in(shift_register_3_out), .clk(clock_1_out), .out(shift_register_3_out));  // open: shift, load, clr, d0, q0, d1, q1, d2, q2, d3, q3, d4, q4, d5, q5
  // AND_Gate and_1 is placed but not wired
  or or_1 (or_1_out, shift_register_2_out, shift_register_2_q0);
  xor xor_1 (xor_1_out, PC_Shift_out, in_5);
  Shift_Register #(.length(6)) shift_register_4 (
    .shift(shift_register_3_out), .in(shift_register_4_out), .clk(clock_1_out), .out(shift_register_4_out),
    .d0(in_1));  // open: load, clr, q0, d1, q1, d2, q2, d3, q3, d4, q4, d5, q5
  Shift_Register #(.length(6)) shift_register_5 (
    .clk(clock_2_out), .q4(shift_register_5_q4), .d5(in_3));  // open: shift, in, out, load, clr, d0, q0, d1, q1, d2, q2, d3, q3, d4, q5
endmodule

module TEST (
  input  in_1,
  input  in_2,
  input  in_3
);

  wire and_1_out, not_1_out, PC_Shift_2_out, PC_Shift_2_q2, PC_Shift_out, xor_1_out;
  wire [31:0] undriven;

  and and_1 (and_1_out, not_1_out, in_3);
  not not_1 (not_1_out, PC_Shift_2_q2);
  Shift_Register #(.length(3)) PC_Shift (
    .shift(and_1_out), .in(PC_Shift_out), .clk(in_1), .out(PC_Shift_out));  // open: load, clr, d0, q0, d1, q1, d2, q2
  Shift_Register #(.length(3)) PC_Shift_2 (
    .shift(xor_1_out), .in(PC_Shift_2_out), .clk(in_1), .out(PC_Shift_2_out), .q2(PC_Shift_2_q2));  // open: load, clr, d0, q0, d1, q1, d2
  xor xor_1 (xor_1_out, PC_Shift_out, in_2);
  // Odd_Parity odd_parity_1 has open pins: in0=undriven[0], in1=undriven[1], in2=undriven[2], in3=undriven[3], in4=undriven[4], in5=undriven[5], in6=undriven[6], in7=undriven[7], in8=undriven[8], in9=undriven[9], in10=undriven[10], in11=undriven[11], in12=undriven[12], in13=undriven[13], in14=undriven[14], in15=undriven[15], in16=undriven[16], in17=undriven[17], in18=undriven[18], in19=undriven[19], in20=undriven[20], in21=undriven[21], in22=undriven[22], in23=undriven[23], in24=undriven[24], in25=undriven[25], in26=undriven[26], in27=undriven[27], in28=undriven[28], in29=undriven[29], in30=undriven[30], in31=undriven[31], out=open
endmodule

module PSW (
  input  [15:0] in_1,
  input  [3:0] in_2,
  output CARRY,
  output borrow
);

  wire [15:0] demultiplexer_1_out2, demultiplexer_1_out4;

  Demultiplexer #(.select(4), .width(16)) demultiplexer_1 (
    .out2(demultiplexer_1_out2), .out4(demultiplexer_1_out4), .in(in_1), .sel(in_2));  // open: out0, out1, out3, out5, out6, out7, out8, out9, out10, out11, out12, out13, out14, out15, en
  Bit_Extender #(.in_width(16), .out_width(1)) bit_extender_1 (.in(demultiplexer_1_out2), .out(CARRY));
  or or_1 (borrow, demultiplexer_1_out4[0], demultiplexer_1_out4[1], demultiplexer_1_out4[2], demultiplexer_1_out4[3], demultiplexer_1_out4[4], demultiplexer_1_out4[5], demultiplexer_1_out4[6], demultiplexer_1_out4[7], demultiplexer_1_out4[8], demultiplexer_1_out4[9], demultiplexer_1_out4[10], demultiplexer_1_out4[11], demultiplexer_1_out4[12], demultiplexer_1_out4[13], demultiplexer_1_out4[14], demultiplexer_1_out4[15]);
endmodule
